// Logisim project mycpu.circ as structural Verilog: 4 circuits, main circuit main
module main (
  input  [15:0] Test_Instruction,
  input  RESET,
  input  CLEAR_ALL_REGS
);

  wire CARRY_FLAG, CLK, control_1_bus_read, control_1_bus_write, REG_WRITE_ENABLE, ZERO_FLAG;
  wire [2:0] ALU_OP, MUX_REG_VALUE, REG_A_SELECT, REG_B_SELECT, REG_SELECT;
  wire [15:0] ALU_OUT, BUS_DATA, control_1_bus_address, multiplexer_1_out, PC, REG_A, REG_B;

  Clock u_CLK (.out(CLK));
  // Probe on REG_A
  // Probe on MUX_REG_VALUE
  Multiplexer #(.select(3), .width(16)) multiplexer_1 (
    .in0(ALU_OUT), .in1(PC), .in2(BUS_DATA), .in3({REG_A[15:8], BUS_DATA[7:0]}),
    .in4({BUS_DATA[7:0], REG_A[7:0]}), .in5(REG_A), .out(multiplexer_1_out), .sel(MUX_REG_VALUE));  // open: in6, in7
  // Probe on multiplexer_1_out
  // Probe on REG_SELECT
  ALU alu1 (.A(REG_A), .B(REG_B), .ALUOP(ALU_OP), .CARRY_FLAG(CARRY_FLAG), .ALU_OUTPUT(ALU_OUT), .ZERO_FLAG(ZERO_FLAG));
  control control_1 (
    .REG_A(REG_A), .RESET(RESET), .CLK(CLK), .ZERO_FLAG(ZERO_FLAG), .CARRY_FLAG(CARRY_FLAG),
    .ALU_OUT(ALU_OUT), .Test_Instruction(Test_Instruction), .BUS_ADDRESS(control_1_bus_address),
    .BUS_DATA(BUS_DATA), .REG_A_SELECT(REG_A_SELECT), .REG_SELECT(REG_SELECT), .REG_B_SELECT(REG_B_SELECT),
    .MUX_REG_VALUE(MUX_REG_VALUE), .BUS_READ(control_1_bus_read), .ALU_OP(ALU_OP),
    .REG_WRITE_ENABLE(REG_WRITE_ENABLE), .BUS_WRITE(control_1_bus_write), .PC_OUT(PC));
  // Probe on control_1_bus_address
  // Probe on PC
  // Probe on ALU_OUT
  // Probe on REG_B_SELECT
  // Probe on REG_A_SELECT
  // Probe on REG_A
  registers registers_1 (
    .clock(CLK), .VALUE(multiplexer_1_out), .REG_WRITE_ENABLE(REG_WRITE_ENABLE), .REG_SELECT(REG_SELECT),
    .REG_A_SELECT(REG_A_SELECT), .REG_SELECT_B(REG_B_SELECT), .CLEAR_ALL_REGS(CLEAR_ALL_REGS), .REG_A(REG_A),
    .REG_B(REG_B));
  // Probe on REG_B
  RAM #(.addrWidth(16), .dataWidth(16), .databus("bidir"), .enables("line")) mainram (
    .addr(control_1_bus_address), .we(control_1_bus_write), .oe(control_1_bus_read), .clk(CLK),
    .data(BUS_DATA));

  // Notes on the sheet:
  //   Test_Instruction: initial=0x10f1
  //   MR + UPPER R
  //   MR + LOWER R
endmodule

module ALU (
  input  [15:0] A,
  input  [15:0] B,
  input  [2:0] ALUOP,
  output CARRY_FLAG,
  output [15:0] ALU_OUTPUT,
  output ZERO_FLAG
);

  wire and_2_out, and_3_out;
  wire [2:0] xnor_1_out, xnor_2_out;
  wire [15:0] adder_1_out, and_1_out, multiplexer_1_out, multiplexer_2_out, not_1_out, or_1_out,
       subtractor_1_out, xor_1_out;

  Multiplexer #(.width(16)) multiplexer_1 (.in0(B), .in1(16'h1), .out(multiplexer_1_out), .sel(and_2_out));
  Multiplexer #(.width(16)) multiplexer_2 (.in0(B), .in1(16'h1), .out(multiplexer_2_out), .sel(and_3_out));
  Adder #(.width(16)) adder_1 (.a(A), .b(multiplexer_1_out), .out(adder_1_out), .cout(CARRY_FLAG));  // open: cin
  Subtractor #(.width(16)) subtractor_1 (.a(A), .b(multiplexer_2_out), .out(subtractor_1_out));  // open: bin, bout
  assign and_1_out = A & B;  // AND_Gate and_1, 16 bits wide
  assign or_1_out = A | B;  // OR_Gate or_1, 16 bits wide
  assign xor_1_out = B ^ A;  // XOR_Gate xor_1, 16 bits wide
  assign not_1_out = ~A;  // NOT_Gate not_1, 16 bits wide
  and and_2 (and_2_out, xnor_1_out[2], xnor_1_out[1], xnor_1_out[0]);
  and and_3 (and_3_out, xnor_2_out[2], xnor_2_out[1], xnor_2_out[0]);
  assign xnor_1_out = ~(ALUOP ^ 3'b111);  // XNOR_Gate xnor_1, 3 bits wide
  assign xnor_2_out = ~(ALUOP ^ 3'b110);  // XNOR_Gate xnor_2, 3 bits wide
  Multiplexer #(.select(3), .width(16)) multiplexer_3 (
    .in0(adder_1_out), .in1(subtractor_1_out), .in2(and_1_out), .in3(or_1_out), .in4(xor_1_out),
    .in5(not_1_out), .in6(subtractor_1_out), .in7(adder_1_out), .out(ALU_OUTPUT), .sel(ALUOP));
  nor nor_1 (ZERO_FLAG, ALU_OUTPUT[0], ALU_OUTPUT[1], ALU_OUTPUT[2], ALU_OUTPUT[3], ALU_OUTPUT[4], ALU_OUTPUT[5], ALU_OUTPUT[6], ALU_OUTPUT[7], ALU_OUTPUT[8], ALU_OUTPUT[9], ALU_OUTPUT[10], ALU_OUTPUT[11], ALU_OUTPUT[12], ALU_OUTPUT[13], ALU_OUTPUT[14], ALU_OUTPUT[15]);

  // Notes on the sheet:
  //   A
  //   B
  //   A
  //   B
  //   0 A+B
  //   1 A-B
  //   2 A AND B
  //   3 A OR B
  //   4 A EXOR B
  //   5 NOT A
  //   6 A-1
  //   7 A+1
endmodule

module registers (
  input  clock,
  input  [15:0] VALUE,
  input  REG_WRITE_ENABLE,
  input  [2:0] REG_SELECT,
  input  [2:0] REG_A_SELECT,
  input  [2:0] REG_SELECT_B,
  input  CLEAR_ALL_REGS,
  output [15:0] REG_A,
  output [15:0] REG_B
);

  wire demultiplexer_1_out0, demultiplexer_1_out1, demultiplexer_1_out2, demultiplexer_1_out3,
       demultiplexer_1_out4, demultiplexer_1_out5, demultiplexer_1_out6, demultiplexer_1_out7;
  wire [15:0] R0_q, R1_q, R2_q, R3_q, R4_q, R5_q, R6_q, R7_q;

  // Probe on VALUE
  Demultiplexer #(.select(3)) demultiplexer_1 (
    .out0(demultiplexer_1_out0), .out1(demultiplexer_1_out1), .out2(demultiplexer_1_out2),
    .out3(demultiplexer_1_out3), .out4(demultiplexer_1_out4), .out5(demultiplexer_1_out5),
    .out6(demultiplexer_1_out6), .out7(demultiplexer_1_out7), .in(REG_WRITE_ENABLE), .sel(REG_SELECT));
  Register #(.trigger("falling"), .width(16)) R0 (
    .D(VALUE), .en(demultiplexer_1_out0), .clk(clock), .Q(R0_q), .clr(CLEAR_ALL_REGS));
  Register #(.trigger("falling"), .width(16)) R2 (
    .D(VALUE), .en(demultiplexer_1_out2), .clk(clock), .Q(R2_q), .clr(CLEAR_ALL_REGS));
  Register #(.trigger("falling"), .width(16)) R4 (
    .D(VALUE), .en(demultiplexer_1_out4), .clk(clock), .Q(R4_q), .clr(CLEAR_ALL_REGS));
  Register #(.trigger("falling"), .width(16)) R6 (
    .D(VALUE), .en(demultiplexer_1_out6), .clk(clock), .Q(R6_q), .clr(CLEAR_ALL_REGS));
  Register #(.trigger("falling"), .width(16)) R1 (
    .D(VALUE), .en(demultiplexer_1_out1), .clk(clock), .Q(R1_q), .clr(CLEAR_ALL_REGS));
  Register #(.trigger("falling"), .width(16)) R3 (
    .D(VALUE), .en(demultiplexer_1_out3), .clk(clock), .Q(R3_q), .clr(CLEAR_ALL_REGS));
  Register #(.trigger("falling"), .width(16)) R5 (
    .D(VALUE), .en(demultiplexer_1_out5), .clk(clock), .Q(R5_q), .clr(CLEAR_ALL_REGS));
  Register #(.trigger("falling"), .width(16)) R7 (
    .D(VALUE), .en(demultiplexer_1_out7), .clk(clock), .Q(R7_q), .clr(CLEAR_ALL_REGS));
  Multiplexer #(.select(3), .width(16)) multiplexer_1 (
    .in0(R0_q), .in1(R1_q), .in2(R2_q), .in3(R3_q), .in4(R4_q), .in5(R5_q), .in6(R6_q), .in7(R7_q),
    .out(REG_A), .sel(REG_A_SELECT));
  Multiplexer #(.select(3), .width(16)) multiplexer_2 (
    .in0(R0_q), .in1(R1_q), .in2(R2_q), .in3(R3_q), .in4(R4_q), .in5(R5_q), .in6(R6_q), .in7(R7_q),
    .out(REG_B), .sel(REG_SELECT_B));
endmodule

module control (
  input  [15:0] REG_A,
  input  RESET,
  input  CLK,
  input  ZERO_FLAG,
  input  CARRY_FLAG,
  input  [15:0] ALU_OUT,
  input  [15:0] Test_Instruction,
  output [15:0] BUS_ADDRESS,
  output [15:0] BUS_DATA,
  output [2:0] REG_A_SELECT,
  output [2:0] REG_SELECT,
  output [2:0] REG_B_SELECT,
  output [2:0] MUX_REG_VALUE,
  output BUS_READ,
  output [2:0] ALU_OP,
  output REG_WRITE_ENABLE,
  output BUS_WRITE,
  output [15:0] PC_OUT
);

  wire and_1_out, GATE_AR, GATE_IR, GATE_PC, LOAD_PC, MUX_AR, not_1_out, SET_REG_A_SELECT_TO_REG_SELECT,
       uc_reset;
  wire [2:0] uc_counter_q;
  wire [3:0] OPCODE;
  wire [5:3] IR_q;
  wire [14:12] microcode_data;
  wire [15:0] multiplexer_1_out;

  Counter #(.max('hffff), .width(16)) PC (
    .clr(1'b0), .load(LOAD_PC), .up(1'b1), .count(GATE_PC), .clk(CLK), .D(REG_A), .Q(PC_OUT));  // open: carry
  Counter #(.max('hffff), .width(16)) IR (
    .clr(1'b0), .load(1'b1), .up(1'b0), .count(GATE_IR), .clk(CLK), .D(Test_Instruction),
    .Q({OPCODE, REG_SELECT, REG_B_SELECT, IR_q, ALU_OP}));  // open: carry
  Multiplexer #(.width(16)) multiplexer_1 (.in0(PC_OUT), .in1(REG_A), .out(multiplexer_1_out), .sel(MUX_AR));
  Multiplexer #(.width(3)) multiplexer_2 (
    .in0(IR_q), .in1(REG_SELECT), .out(REG_A_SELECT), .sel(SET_REG_A_SELECT_TO_REG_SELECT));
  Counter #(.max('hffff), .width(16)) AR (
    .clr(1'b0), .load(1'b1), .count(GATE_AR), .clk(CLK), .D(multiplexer_1_out));  // open: up, carry, Q
  not not_1 (not_1_out, CLK);
  and and_1 (and_1_out, not_1_out, uc_reset);
  Counter #(.max('h7), .width(3)) uc_counter (
    .clr(and_1_out), .load(1'b0), .up(1'b1), .count(1'b1), .clk(CLK), .D(3'b000), .Q(uc_counter_q));  // open: carry
  Register #(.width(16)) AR_REG (.D(multiplexer_1_out), .en(GATE_AR), .clk(CLK), .Q(BUS_ADDRESS));  // open: clr
  // Probe on ALU_OUT
  // Probe on {OPCODE, uc_counter_q}
  ROM #(.addrWidth(7), .dataWidth(16)) microcode (
    .addr({OPCODE, uc_counter_q}),
    .data({GATE_IR, microcode_data, SET_REG_A_SELECT_TO_REG_SELECT, MUX_REG_VALUE, GATE_AR, REG_WRITE_ENABLE, MUX_AR, BUS_WRITE, BUS_READ, LOAD_PC, GATE_PC, uc_reset}));
  Counter #(.max('hffff), .width(16)) DR ();  // open: clr, load, up, count, clk, D, carry, Q
  // Probe on {GATE_IR, microcode_data, SET_REG_A_SELECT_TO_REG_SELECT, MUX_REG_VALUE, GATE_AR, REG_WRITE_ENABLE, MUX_AR, BUS_WRITE, BUS_READ, LOAD_PC, GATE_PC, uc_reset}

  assign BUS_DATA = Test_Instruction;

  // Notes on the sheet:
  //   Test_Instruction: initial=0x10f1
  //   contents of microcode (hex, n*v repeats v):
  //   8088 343 6*0 8088 c43 6*0 8088 7*0 8088 7*0 8088 3000 6*0 8088 7*0 8088 7*0 8088 7*0 8088 7*0 8088
  //   7*0 8088 7*0 8088 7*0 8088 7*0 8088 7*0 8088 7*0 8088
endmodule
